// Digital circuit circuito0.dig as structural Verilog
module circuito0 (
  input  D,
  input  C,
  input  B,
  input  A,
  output f
);

  wire and_1_out, and_2_out;

  and and_1 (and_1_out, ~B, ~D);  // And
  and and_2 (and_2_out, D, ~C);  // And
  or or_1 (f, and_1_out, and_2_out);
endmodule

/* Test case Teste:
D C B A f 

 0 0 0 0 1
 0 0 0 1 1
 0 0 1 0 0
 0 0 1 1 0
 0 1 0 0 1
 0 1 0 1 1
 0 1 1 0 0
 0 1 1 1 0
 1 0 0 0 1
 1 0 0 1 1
 1 0 1 0 1
 1 0 1 1 1
 1 1 0 0 0
 1 1 0 1 0
 1 1 1 0 0
 1 1 1 1 0
*/
