// Digital circuit circuito1.dig as structural Verilog
module circuito1 (
  input  A,
  input  B,
  input  S,
  output Y
);

  wire fgnfet_2_s, fgnfet_4_s, fgnfet_6_s, fgpfet_1_d, fgpfet_2_d, fgpfet_3_d;

  FGPFET fgpfet_1 (.G(S), .S(1'b1), .D(fgpfet_1_d));
  FGNFET fgnfet_1 (.G(S), .D(fgpfet_1_d), .S(1'b0));
  FGPFET fgpfet_2 (.G(A), .S(1'b1), .D(fgpfet_2_d));
  FGNFET fgnfet_2 (.G(fgpfet_1_d), .D(fgpfet_2_d), .S(fgnfet_2_s));
  FGNFET fgnfet_3 (.G(A), .D(fgnfet_2_s), .S(1'b0));
  FGPFET fgpfet_3 (.G(B), .S(1'b1), .D(fgpfet_3_d));
  FGNFET fgnfet_4 (.G(S), .D(fgpfet_3_d), .S(fgnfet_4_s));
  FGNFET fgnfet_5 (.G(B), .D(fgnfet_4_s), .S(1'b0));
  FGPFET fgpfet_4 (.G(fgpfet_1_d), .S(1'b1), .D(fgpfet_2_d));
  FGPFET fgpfet_5 (.G(S), .S(1'b1), .D(fgpfet_3_d));
  FGPFET fgpfet_6 (.G(fgpfet_3_d), .S(1'b1), .D(Y));
  FGPFET fgpfet_7 (.G(fgpfet_2_d), .S(1'b1), .D(Y));
  FGNFET fgnfet_6 (.G(fgpfet_2_d), .D(Y), .S(fgnfet_6_s));
  FGNFET fgnfet_7 (.G(fgpfet_3_d), .D(fgnfet_6_s), .S(1'b0));
endmodule
