// Digital circuit circuito2.dig as structural Verilog
module circuito2 (
  input  B,
  input  A,
  input  S,
  output Y
);

  wire fgpfet_1_d;

  FGPFET fgpfet_1 (.G(S), .S(1'b1), .D(fgpfet_1_d));
  FGNFET fgnfet_1 (.G(S), .D(fgpfet_1_d), .S(1'b0));
  TransGate transgate_1 (.A(S), .nA(fgpfet_1_d), .out1(B), .out2(Y));
  TransGate transgate_2 (.A(fgpfet_1_d), .nA(S), .out1(A), .out2(Y));
endmodule
