// Digital circuit circuito3.dig as structural Verilog
module circuito3 (
  input  A,
  input  B,
  input  S,
  output Y
);

  wire and_1_out, and_2_out;

  and and_1 (and_1_out, ~S, A);  // And
  and and_2 (and_2_out, S, B);
  or or_1 (Y, and_1_out, and_2_out);
endmodule
