// Digital circuit circuito5.dig as structural Verilog
module circuito5 (
  input  D,
  input  C,
  input  B,
  input  A,
  output f
);

  Multiplexer multiplexer_1 ();  // open: sel, in_0, in_1, out
  Multiplexer #(.Selector_Bits(3)) multiplexer_2 ();  // open: sel, in_0, in_1, in_2, in_3, in_4, in_5, in_6, in_7, out
  Multiplexer #(.Selector_Bits(3)) multiplexer_3 ();  // open: sel, in_0, in_1, in_2, in_3, in_4, in_5, in_6, in_7, out
endmodule
