// Digital circuit circuito.dig as structural Verilog
module circuito (
  input  A0,
  input  B0,
  input  A1,
  input  B1,
  output S0,
  output S1,
  output S2
);

  wire nand_1_out, nand_2_out, nand_3_out, nand_4_out, nand_5_out, nand_6_out, nand_7_out, nand_8_out,
       nand_9_out, nand_10_out, nand_11_out, nand_12_out, nand_13_out, nand_14_out, nand_16_out;

  nand nand_1 (nand_1_out, A0, B0);
  nand nand_2 (nand_2_out, A1, B1);
  nand nand_3 (nand_3_out, A0, nand_1_out);
  nand nand_4 (nand_4_out, nand_1_out, B0);
  nand nand_5 (nand_5_out, A1, nand_2_out);
  nand nand_6 (nand_6_out, nand_2_out, B1);
  nand nand_7 (nand_7_out, nand_5_out, nand_6_out);
  nand nand_8 (nand_8_out, nand_3_out, nand_4_out);
  nand nand_9 (nand_9_out, nand_11_out, nand_1_out);
  nand nand_10 (nand_10_out, nand_9_out, nand_7_out);
  nand nand_11 (nand_11_out, 1'b0, nand_8_out);
  nand nand_12 (nand_12_out, nand_9_out, nand_10_out);
  nand nand_13 (nand_13_out, 1'b0, nand_11_out);
  nand nand_14 (nand_14_out, nand_11_out, nand_8_out);
  nand nand_15 (S2, nand_10_out, nand_2_out);
  nand nand_16 (nand_16_out, nand_10_out, nand_7_out);
  nand nand_17 (S1, nand_12_out, nand_16_out);
  nand nand_18 (S0, nand_13_out, nand_14_out);

  // Notes on the sheet:
  //   P1
  //   P10
  //   P9
endmodule
