// Digital circuit ex3.dig as structural Verilog
module ex3 (
  input  A,
  input  B,
  input  C,
  input  D,
  output F,
  output G,
  output H
);

  wire and_1_out, and_2_out, not_1_out, not_2_out;

  not not_1 (not_1_out, A);
  not not_2 (not_2_out, B);
  and and_1 (and_1_out, not_1_out, not_2_out);
  and and_2 (and_2_out, B, C);
  and and_3 (G, D, C);
  or or_1 (F, and_1_out, and_2_out);

  assign H = D;
endmodule
