// Digital circuit ex4_v2.dig as structural Verilog
module ex4_v2 (
  input  A,
  input  B,
  input  C,
  input  D,
  output G,
  output F,
  output H
);

  wire and_1_out, and_2_out, and_3_out, and_4_out, not_1_out, not_2_out, not_3_out, not_4_out, or_1_out,
       or_2_out, or_3_out, or_5_out;

  not not_1 (not_1_out, A);
  not not_2 (not_2_out, B);
  not not_3 (not_3_out, C);
  or or_1 (or_1_out, A, C);
  and and_1 (and_1_out, A, not_2_out);
  and and_2 (and_2_out, not_1_out, B);
  and and_3 (and_3_out, not_1_out, C);
  or or_2 (or_2_out, A, not_2_out);
  or or_3 (or_3_out, not_3_out, D);
  not not_4 (not_4_out, A);
  and and_4 (and_4_out, B, or_1_out);
  or or_4 (G, and_1_out, and_2_out, and_3_out);
  and and_5 (H, or_2_out, or_3_out);
  or or_5 (or_5_out, C, not_4_out);
  and and_6 (F, or_5_out, and_4_out);
endmodule
