// Digital circuit ex5_v2.dig as structural Verilog
module ex5_v2 (
  input  A,
  input  B,
  input  C,
  input  D,
  output F,
  output G,
  output H
);

  wire and_1_out, and_2_out, and_3_out, not_1_out, not_2_out, not_3_out;

  not not_1 (not_1_out, A);
  not not_2 (not_2_out, C);
  and and_1 (and_1_out, B, C);
  and and_2 (and_2_out, B, D);
  and and_3 (and_3_out, not_2_out, D);
  and and_4 (G, not_1_out, B, not_2_out);
  or or_1 (H, not_3_out, and_2_out, and_3_out);
  or or_2 (F, A, and_1_out);
  not not_3 (not_3_out, G);
endmodule
