// Digital circuit ex5_v3.dig as structural Verilog
module ex5_v3 (
  input  A,
  input  B,
  input  C,
  input  D,
  output F,
  output G,
  output H
);

  wire and_1_out, and_2_out, and_3_out, and_4_out, not_1_out, not_2_out, not_3_out, not_4_out, or_1_out;

  not not_1 (not_1_out, A);
  not not_2 (not_2_out, C);
  not not_3 (not_3_out, B);
  not not_4 (not_4_out, C);
  and and_1 (and_1_out, B, C);
  or or_1 (or_1_out, not_1_out, B);
  or or_2 (F, A, and_1_out);
  and and_2 (and_2_out, A, not_3_out, not_4_out);
  and and_3 (and_3_out, B, D);
  and and_4 (and_4_out, not_4_out, D);
  and and_5 (G, not_2_out, or_1_out);
  or or_3 (H, and_2_out, and_3_out, and_4_out);
endmodule
