// Digital circuit 3_somador4b_rc.dig as structural Verilog
module _3_somador4b_rc (
  input  [3:0] B,
  input  [3:0] A,
  input  Cin,
  output [3:0] sum,
  output Cout
);

  somador2b_rc #(.applicationType("IVERILOG"), .CodeFile("/home/balbertini/GIT/gitlab.usp.br/pcs3115/exercicios/a08_verilog/3_somador4b_rc.v")) u_somador2b_rc (
    .a(A), .b(B), .cin(Cin), .sum(sum), .cout(Cout));
endmodule
