// Digital circuit C.dig as structural Verilog
module C (
  input  A,
  input  B,
  input  C,
  input  D,
  output Y
);

  wire and_1_out, or_1_out;

  and and_1 (and_1_out, B, D);
  or or_1 (or_1_out, B, D);
  Multiplexer #(.Selector_Bits(2)) multiplexer_1 (
    .sel({C, A}), .in_0(and_1_out), .in_1(B), .in_2(or_1_out), .in_3(1'b1), .out(Y));
endmodule
