// Digital circuit 01.dig as structural Verilog
module _01 (
  input  A,
  input  B,
  input  S,
  output Y
);

  wire nand_1_out, nand_2_out, not_1_out;

  not not_1 (not_1_out, S);
  nand nand_1 (nand_1_out, not_1_out, A);
  nand nand_2 (nand_2_out, B, S);
  nand nand_3 (Y, nand_1_out, nand_2_out);
endmodule
