// Digital circuit 05.dig as structural Verilog
module _05 (
  input  D,
  input  C,
  input  B,
  input  A,
  output f
);

  wire multiplexer_1_out, multiplexer_2_out;

  Multiplexer #(.Selector_Bits(3)) multiplexer_1 (
    .sel({B, C, D}), .in_0(1'b1), .in_1(1'b1), .in_2(1'b1), .in_3(1'b0), .in_4(1'b0), .in_5(1'b1),
    .in_6(1'b0), .in_7(1'b0), .out(multiplexer_1_out));
  Multiplexer #(.Selector_Bits(3)) multiplexer_2 (
    .sel({B, C, D}), .in_0(1'b1), .in_1(1'b1), .in_2(1'b1), .in_3(1'b0), .in_4(1'b0), .in_5(1'b1),
    .in_6(1'b0), .in_7(1'b0), .out(multiplexer_2_out));
  Multiplexer multiplexer_3 (.sel(A), .in_0(multiplexer_1_out), .in_1(multiplexer_2_out), .out(f));
endmodule
