// Digital circuit circuito4.dig as structural Verilog
module circuito4 (
  input  D,
  input  C,
  input  B,
  input  A,
  output f
);

  Multiplexer #(.Selector_Bits(4)) multiplexer_1 (
    .sel({A, B, C, D}), .in_0(1'b1), .in_1(1'b1), .in_2(1'b1), .in_3(1'b0), .in_4(1'b0), .in_5(1'b1),
    .in_6(1'b0), .in_7(1'b0), .in_8(1'b1), .in_9(1'b1), .in_10(1'b1), .in_11(1'b0), .in_12(1'b0),
    .in_13(1'b1), .in_14(1'b0), .in_15(1'b0), .out(f));
endmodule

/* Test case Teste:
D C B A f 

 0 0 0 0 1
 0 0 0 1 1
 0 0 1 0 0
 0 0 1 1 0
 0 1 0 0 1
 0 1 0 1 1
 0 1 1 0 0
 0 1 1 1 0
 1 0 0 0 1
 1 0 0 1 1
 1 0 1 0 1
 1 0 1 1 1
 1 1 0 0 0
 1 1 0 1 0
 1 1 1 0 0
 1 1 1 1 0
*/
