// Digital circuit circuito6.dig as structural Verilog
module circuito6 (
  input  D,
  input  C,
  input  B,
  input  A,
  output f
);

  Multiplexer multiplexer_1 ();  // open: sel, in_0, in_1, out
  Multiplexer #(.Selector_Bits(2)) multiplexer_2 ();  // open: sel, in_0, in_1, in_2, in_3, out
  Multiplexer #(.Selector_Bits(2)) multiplexer_3 ();  // open: sel, in_0, in_1, in_2, in_3, out
endmodule
