// Digital circuit circuito7.dig as structural Verilog
module circuito7 (
  input  D,
  input  C,
  input  B,
  input  A,
  output f
);

  wire and_1_out, and_2_out, not_1_out, not_2_out, not_3_out;

  not not_1 (not_1_out, B);
  not not_2 (not_2_out, C);
  not not_3 (not_3_out, D);
  and and_1 (and_1_out, not_3_out, not_1_out);
  and and_2 (and_2_out, not_2_out, not_1_out);
  Multiplexer multiplexer_1 (.sel(A), .in_0(and_1_out), .in_1(and_2_out), .out(f));
endmodule
