// Digital circuit ex1.dig as structural Verilog
module ex1 (
  input  B,
  input  A,
  output F,
  output G,
  output H,
  output I,
  output J
);

  wire not_1_out;

  not not_1 (not_1_out, A);
  and and_1 (I, not_1_out, B);

  assign F = B;
  assign G = A;
  assign H = A;
  assign J = A;
endmodule
