// Digital circuit ex2.dig as structural Verilog
module ex2 (
  input  A,
  input  B,
  input  C,
  output F,
  output G,
  output H
);

  wire and_2_out, not_1_out, not_2_out;

  not not_1 (not_1_out, A);
  not not_2 (not_2_out, B);
  and and_1 (F, not_1_out, not_2_out);
  or or_1 (G, A, B);
  and and_2 (and_2_out, not_2_out, C);
  or or_2 (H, not_1_out, and_2_out);
endmodule
