// Digital circuit ex4.dig as structural Verilog
module ex4 (
  input  A,
  input  B,
  input  C,
  input  D,
  output G,
  output F,
  output H
);

  wire and_1_out, and_2_out, and_3_out, and_4_out, not_1_out, not_2_out, not_3_out, or_1_out, or_2_out;

  not not_1 (not_1_out, A);
  not not_2 (not_2_out, B);
  not not_3 (not_3_out, C);
  and and_1 (and_1_out, A, B);
  and and_2 (and_2_out, A, not_2_out);
  and and_3 (and_3_out, not_1_out, B);
  and and_4 (and_4_out, not_1_out, C);
  or or_1 (or_1_out, A, not_2_out);
  or or_2 (or_2_out, not_3_out, D);
  or or_3 (F, and_1_out, C);
  or or_4 (G, and_2_out, and_3_out, and_4_out);
  and and_5 (H, or_1_out, or_2_out);
endmodule
