// Digital circuit 1_portae.dig as structural Verilog
module _1_portae (
  input  A,
  input  B,
  output Y
);

  porta_e #(.applicationType("IVERILOG")) u_porta_e (.a(A), .b(B), .y(Y));
endmodule

/* Code of porta_e:
module porta_e(
    input a,
    input b,
    output y
);
    assign y = a & b;
endmodule
*/
