// Digital circuit 2_mux2to1.dig as structural Verilog
module _2_mux2to1 (
  input  B,
  input  sel,
  input  A,
  output Y
);

  mux2to1 #(.applicationType("IVERILOG"), .CodeFile("/home/balbertini/GIT/gitlab.usp.br/pcs3115/exercicios/a08_verilog/2_mux2to1.v")) u_mux2to1 (
    .a(A), .b(B), .sel(sel), .y(Y));
endmodule
