// Digital circuit primo.dig as structural Verilog
module primo (
  input  b2,
  input  b3,
  input  b0,
  input  b1,
  output S
);

  wire and_1_out, and_2_out, and_3_out, not_1_out, not_2_out, not_3_out, or_1_out;

  not not_1 (not_1_out, b2);
  not not_2 (not_2_out, b3);
  not not_3 (not_3_out, b1);
  or or_1 (or_1_out, not_1_out, not_2_out);
  and and_1 (and_1_out, b2, b0, not_3_out);
  and and_2 (and_2_out, not_1_out, not_2_out, b1);
  and and_3 (and_3_out, or_1_out, b0, b1);
  or or_2 (S, and_3_out, and_1_out, and_2_out);
endmodule
