// Digital circuit A.dig as structural Verilog
module A (
  input  A,
  input  B,
  input  C,
  output f
);

  wire and_1_out, and_2_out, or_1_out;

  or or_1 (or_1_out, B, C);
  and and_1 (and_1_out, B, C);
  and and_2 (and_2_out, A, or_1_out);
  or or_2 (f, and_2_out, and_1_out);
endmodule
